# Fritzing sketch ExternalDashboardV2 (saved by Fritzing 0.9.9b)
circuit board: 8.40082cm x 4.34622cm
breadboards: 1

parts:
  Part2 = HC-SR501 Body Sensor Module
  J1 = Raspberry Pi Header 40pin [package=THT]
  R5 = Resistor [tolerance=±5% power=0.25 resistance=680 package=THT]
  R6 = Resistor [tolerance=±5% power=0.25 resistance=10k package=THT]
  R7 = Resistor [tolerance=±5% power=0.25 resistance=10k package=THT]
  DHT1 = DHT11 Humitidy and Temperature Sensor
  LCD1602_-_RGB = LCD1602-I2C
  LED1 = smd LED [color="Blue (470nm)" package="1206 [SMD]"]

nets:
  VCC: Part2.VCC, J1.5V, R6.Pin_1, R7.Pin_1, DHT1.VDD, LCD1602_-_RGB.VCC
  N1: Part2.OUT, J1.IO23
  GND: Part2.GND, J1.GND, DHT1.GND, LCD1602_-_RGB.GND, LED1.cathode
  N2: J1.GPIO2, R7.Pin_0, LCD1602_-_RGB.SDA
  N3: J1.IO3, R6.Pin_0, LCD1602_-_RGB.SCL
  N4: J1.IO24, R5.Pin_1
  N5: J1.IO25, DHT1.DATA
  N6: R5.Pin_0, LED1.anode

notes:
  Flight Control Dash Display
  Jason Brooks
  www.muckypaws.com

custom parts:
  HC-SR501 Body Sensor Module: Pyroelectric Infrared PIR Motion Sensor Detector Module
  Raspberry Pi Header 40pin: Raspberry Pi 40 pin header - for creating your own shields. (Mar 2020, bb: make breadboard friendly (.4in pin spacing) and add labels. Schematic add labels. PCB make oblong pins to allow routing traces between the pins.)
  DHT11 Humitidy and Temperature Sensor: DHT11 Humidity and Temperature Sensor
  LCD1602-I2C: A standard character display, usually with 2x16 characters. Comes in many colors with LCM1602 IIC attached.
